# Fritzing sketch Final_Project (saved by Fritzing 0.9.5d)
breadboards: 1

parts:
  Raspberry_Pi_1 = Raspberry Pi 3 [part_number=RPI-3-V1.2]
  IC1 = L293D [package=THT]
  M1 = DC Motor
  M2 = DC Motor
  M3 = DC Motor
  U1 = LCD-16X2 [package=lcd-16x2]  # not connected
  RE1 = Rotary Encoder [package=THT]
  IC2 = L293D [package=THT]

nets:
  N1: Raspberry_Pi_1.GPIO2, RE1.EncoderPinA
  N2: Raspberry_Pi_1.GPIO3, RE1.EncoderPinC
  N3: Raspberry_Pi_1.GPIO4, RE1.EncoderPinB
  N4: Raspberry_Pi_1.GPIO6, IC1.Enable_1
  N5: Raspberry_Pi_1.GPIO19, IC2.Enable_1
  N6: Raspberry_Pi_1.GPIO23, IC1.Enable_2
  N7: IC1.In_1, IC2.In_1
  N8: IC1.Out_1_(_Controlled_by_Enable_1_), M3.pin_1
  N9: IC1.0V, IC1.In_3, IC2.0V
  N10: IC1.Out_2_(_Controlled_by_Enable_1_), M3.pin_2
  N11: IC1.In_2, IC1.+Vmotor, IC2.In_2, IC2.+Vmotor
  N12: IC1.Out_3_(_Controlled_by_Enable_2_), M1.pin_2
  N13: IC1.Out_4_(_Controlled_by_Enable_2_), M1.pin_1
  N14: IC1.In_4, IC1.+V, IC2.+V
  N15: M2.pin_1, IC2.Out_2_(_Controlled_by_Enable_1_)
  N16: M2.pin_2, IC2.Out_1_(_Controlled_by_Enable_1_)
